# Fritzing sketch Clase 3 (Entradas PWM) (saved by Fritzing 0.9.3b)
breadboards: 1

parts:
  U1 = NodeMCU V1.0
  R1 = Rotary Potentiometer (Small) [maximum_resistance=100kΩ package=THT]
  LED1 = LED - 5mm [color="Red (633nm)" package="5 mm [THT]"]
  R2 = Resistor [tolerance=±5% resistance=220 package=THT]

nets:
  N1: U1.D4, LED1.anode
  N2: U1.3V3, R1.leg2
  N3: U1.GND, R1.leg1, R2.Pin_0
  N4: U1.A0, R1.wiper
  N5: LED1.cathode, R2.Pin_1

custom parts:
  NodeMCU V1.0: ESP8266 based NodeMCU
