# Fritzing sketch Clase 4 (Pulsador) (saved by Fritzing 0.9.3b)
breadboards: 1

parts:
  S1 = Pushbutton [package="[THT]"]
  S2 = Pushbutton [package="[THT]"]
  LED1 = LED - 5mm [color="Red (633nm)" package="5 mm [THT]"]
  R1 = Resistor [tolerance=±5% resistance=220 package=THT]
  R2 = Resistor [tolerance=±5% resistance=10k package=THT]
  LED2 = LED - 5mm [color="Blue (470nm)" package="5 mm [THT]"]
  LED3 = LED - 5mm [color="Green (555nm)" package="5 mm [THT]"]
  R3 = Resistor [tolerance=±5% resistance=220 package=THT]
  R4 = Resistor [tolerance=±5% resistance=220 package=THT]
  U1 = NodeMCU V1.0

nets:
  N1: S1.Pin_1, S1.Pin_2, R2.Pin_1, U1.D2
  N2: S1.Pin_3, S1.Pin_4, U1.3V3
  N3: S2.Pin_1, S2.Pin_2, U1.D1
  N4: S2.Pin_3, S2.Pin_4
  N5: LED1.cathode, R1.Pin_1
  N6: LED1.anode, U1.D0
  N7: R1.Pin_0, R2.Pin_0, R3.Pin_0, R4.Pin_0, U1.GND
  N8: LED2.cathode, R3.Pin_1
  N9: LED2.anode, U1.D4
  N10: LED3.cathode, R4.Pin_1
  N11: LED3.anode, U1.D6

custom parts:
  NodeMCU V1.0: ESP8266 based NodeMCU
