# Fritzing sketch Clase 5 (Ultrasonico) (saved by Fritzing 0.9.3b)
breadboards: 1

parts:
  U1 = NodeMCU V1.0
  Componente1 = HC-SR04
  R1 = Resistor [tolerance=±5% resistance=1.5k package=THT]
  R2 = Resistor [tolerance=±5% resistance=1.5k package=THT]

nets:
  GND: U1.GND, Componente1.Gnd, R2.Pin_1
  N1: U1.D5, U1.D6, R1.Pin_1, R2.Pin_0
  VIN: U1.Vin, Componente1.Vcc
  N2: Componente1.Echo, R1.Pin_0

custom parts:
  NodeMCU V1.0: ESP8266 based NodeMCU
  HC-SR04: HC-SR04 ultrasonic distance sensor
