# Fritzing sketch Clase 6.1 (LM35) (saved by Fritzing 0.9.3b)
breadboards: 1

parts:
  U1 = NodeMCU V1.0
  T1 = LM35 Temperature Sensor [package="TO92 [THT]"]

nets:
  GND: U1.GND, T1.GND
  N1: U1.Vin, T1.+Vs
  N2: U1.A0, T1.Vout

custom parts:
  NodeMCU V1.0: ESP8266 based NodeMCU
